// Logisim project main-circuit.circ as structural Verilog
module D_Latch (
  input  D,
  input  Enable,
  output Q,
  output Q_prime
);

  wire nand_1_out, nand_2_out, not_1_out;

  nand nand_1 (nand_1_out, D, Enable);
  nand nand_2 (nand_2_out, Enable, not_1_out);
  not not_1 (not_1_out, D);
  nand nand_3 (Q, nand_1_out, Q_prime);
  nand nand_4 (Q_prime, Q, nand_2_out);
endmodule

module D_FF (
  input  D,
  input  Clk,
  output Q
);

  wire d_latch_1_q, not_1_out;

  D_Latch d_latch_1 (.D(D), .Enable(not_1_out), .Q(d_latch_1_q));  // open: Q_prime
  not not_1 (not_1_out, Clk);
  D_Latch d_latch_2 (.D(d_latch_1_q), .Enable(Clk), .Q(Q));  // open: Q_prime
endmodule

module _16_bit_register (
  input  Clk,
  input  Write_En,
  input  Clear,
  input  [15:0] Input,
  output [15:0] Output
);

  wire and_1_out, and_2_out, and_3_out, and_4_out, and_5_out, and_6_out, and_7_out, and_8_out, and_9_out,
       and_10_out, and_11_out, and_12_out, and_13_out, and_14_out, and_15_out, and_16_out, and_17_out,
       and_18_out, and_19_out, and_20_out, and_21_out, and_22_out, and_23_out, and_24_out, and_25_out,
       and_26_out, and_27_out, and_28_out, and_29_out, and_30_out, and_31_out, and_32_out, not_1_out,
       not_2_out, or_1_out, or_2_out, or_3_out, or_4_out, or_5_out, or_6_out, or_7_out, or_8_out, or_9_out,
       or_10_out, or_11_out, or_12_out, or_13_out, or_14_out, or_15_out, or_16_out;

  not not_1 (not_1_out, Clear);
  not not_2 (not_2_out, Write_En);
  and and_1 (and_1_out, Input[7], Write_En, not_1_out);
  and and_2 (and_2_out, Input[6], Write_En, not_1_out);
  and and_3 (and_3_out, Input[5], Write_En, not_1_out);
  and and_4 (and_4_out, Input[4], Write_En, not_1_out);
  and and_5 (and_5_out, Input[3], Write_En, not_1_out);
  and and_6 (and_6_out, Input[2], Write_En, not_1_out);
  and and_7 (and_7_out, Input[1], Write_En, not_1_out);
  and and_8 (and_8_out, Input[0], Write_En, not_1_out);
  and and_9 (and_9_out, Input[15], Write_En, not_1_out);
  and and_10 (and_10_out, Input[14], Write_En, not_1_out);
  and and_11 (and_11_out, Input[13], Write_En, not_1_out);
  and and_12 (and_12_out, Input[12], Write_En, not_1_out);
  and and_13 (and_13_out, Input[11], Write_En, not_1_out);
  and and_14 (and_14_out, Input[10], Write_En, not_1_out);
  and and_15 (and_15_out, Input[9], Write_En, not_1_out);
  and and_16 (and_16_out, Input[8], Write_En, not_1_out);
  and and_17 (and_17_out, not_2_out, not_1_out, Output[7]);
  and and_18 (and_18_out, not_2_out, not_1_out, Output[6]);
  and and_19 (and_19_out, not_2_out, not_1_out, Output[5]);
  and and_20 (and_20_out, not_2_out, not_1_out, Output[4]);
  and and_21 (and_21_out, not_2_out, not_1_out, Output[3]);
  and and_22 (and_22_out, not_2_out, not_1_out, Output[2]);
  and and_23 (and_23_out, not_2_out, not_1_out, Output[1]);
  and and_24 (and_24_out, not_2_out, not_1_out, Output[0]);
  and and_25 (and_25_out, not_2_out, not_1_out, Output[15]);
  and and_26 (and_26_out, not_2_out, not_1_out, Output[14]);
  and and_27 (and_27_out, not_2_out, not_1_out, Output[13]);
  and and_28 (and_28_out, not_2_out, not_1_out, Output[12]);
  and and_29 (and_29_out, not_2_out, not_1_out, Output[11]);
  and and_30 (and_30_out, not_2_out, not_1_out, Output[10]);
  and and_31 (and_31_out, not_2_out, not_1_out, Output[9]);
  and and_32 (and_32_out, not_2_out, not_1_out, Output[8]);
  or or_1 (or_1_out, and_1_out, and_17_out);
  or or_2 (or_2_out, and_2_out, and_18_out);
  or or_3 (or_3_out, and_3_out, and_19_out);
  or or_4 (or_4_out, and_4_out, and_20_out);
  or or_5 (or_5_out, and_5_out, and_21_out);
  or or_6 (or_6_out, and_6_out, and_22_out);
  or or_7 (or_7_out, and_7_out, and_23_out);
  or or_8 (or_8_out, and_8_out, and_24_out);
  or or_9 (or_9_out, and_9_out, and_25_out);
  or or_10 (or_10_out, and_10_out, and_26_out);
  or or_11 (or_11_out, and_11_out, and_27_out);
  or or_12 (or_12_out, and_12_out, and_28_out);
  or or_13 (or_13_out, and_13_out, and_29_out);
  or or_14 (or_14_out, and_14_out, and_30_out);
  or or_15 (or_15_out, and_15_out, and_31_out);
  or or_16 (or_16_out, and_16_out, and_32_out);
  D_FF d_ff_1 (.D(or_1_out), .Clk(Clk), .Q(Output[7]));
  D_FF d_ff_2 (.D(or_2_out), .Clk(Clk), .Q(Output[6]));
  D_FF d_ff_3 (.D(or_3_out), .Clk(Clk), .Q(Output[5]));
  D_FF d_ff_4 (.D(or_4_out), .Clk(Clk), .Q(Output[4]));
  D_FF d_ff_5 (.D(or_5_out), .Clk(Clk), .Q(Output[3]));
  D_FF d_ff_6 (.D(or_6_out), .Clk(Clk), .Q(Output[2]));
  D_FF d_ff_7 (.D(or_7_out), .Clk(Clk), .Q(Output[1]));
  D_FF d_ff_8 (.D(or_8_out), .Clk(Clk), .Q(Output[0]));
  D_FF d_ff_9 (.D(or_9_out), .Clk(Clk), .Q(Output[15]));
  D_FF d_ff_10 (.D(or_10_out), .Clk(Clk), .Q(Output[14]));
  D_FF d_ff_11 (.D(or_11_out), .Clk(Clk), .Q(Output[13]));
  D_FF d_ff_12 (.D(or_12_out), .Clk(Clk), .Q(Output[12]));
  D_FF d_ff_13 (.D(or_13_out), .Clk(Clk), .Q(Output[11]));
  D_FF d_ff_14 (.D(or_14_out), .Clk(Clk), .Q(Output[10]));
  D_FF d_ff_15 (.D(or_15_out), .Clk(Clk), .Q(Output[9]));
  D_FF d_ff_16 (.D(or_16_out), .Clk(Clk), .Q(Output[8]));

  // Notes on the sheet:
  //   Little Endian
endmodule

module Test_Register (
  input  Write_En,
  input  Clear,
  input  [7:0] Input,
  output [7:0] Output
);

  wire Clk_out;

  Clock Clk (.out(Clk_out));
  // _16_bit_register 16_bit_register_1: pin names not known; wires that end beside it: Clk_out, Write_En, Clear, Input, Output
endmodule

module _2_x_4_decoder (
  input  En,
  input  A,
  input  B,
  output D0,
  output D1,
  output D2,
  output D3
);

  wire not_1_out, not_2_out;

  not not_1 (not_1_out, A);
  not not_2 (not_2_out, B);
  and and_1 (D0, not_1_out, En, not_2_out);
  and and_2 (D1, not_1_out, En, B);
  and and_3 (D2, A, En, not_2_out);
  and and_4 (D3, A, En, B);
endmodule

module _3_x_8_decoder (
  input  En,
  input  A2,
  input  A1,
  input  A0,
  output D0,
  output D1,
  output D2,
  output D3,
  output D4,
  output D5,
  output D6,
  output D7
);

  wire and_1_out, and_2_out, not_1_out;

  not not_1 (not_1_out, A2);
  and and_1 (and_1_out, A2, En);
  and and_2 (and_2_out, En, not_1_out);
  _2_x_4_decoder u_2_x_4_decoder_1 (.En(and_2_out), .A(A1), .B(A0), .D0(D0), .D1(D1), .D2(D2), .D3(D3));
  _2_x_4_decoder u_2_x_4_decoder_2 (.En(and_1_out), .A(A1), .B(A0), .D0(D4), .D1(D5), .D2(D6), .D3(D7));
endmodule

module _4_x_16_decoder (
  input  Enable,
  input  A4,
  input  A2,
  input  A1,
  input  A0,
  output [15:0] Output
);

  wire and_1_out, and_2_out, not_1_out;

  not not_1 (not_1_out, A4);
  and and_1 (and_1_out, Enable, A4);
  and and_2 (and_2_out, Enable, not_1_out);
  _3_x_8_decoder u_3_x_8_decoder_1 (
    .A2(A2), .A1(A1), .A0(A0), .En(and_2_out), .D0(Output[0]), .D1(Output[1]), .D2(Output[2]),
    .D3(Output[3]), .D4(Output[4]), .D5(Output[5]), .D6(Output[6]), .D7(Output[7]));
  _3_x_8_decoder u_3_x_8_decoder_2 (
    .A2(A2), .A1(A1), .A0(A0), .En(and_1_out), .D0(Output[8]), .D1(Output[9]), .D2(Output[10]),
    .D3(Output[11]), .D4(Output[12]), .D5(Output[13]), .D6(Output[14]), .D7(Output[15]));
endmodule

module _5_x_32_decoder (
  input  Enable,
  input  A4,
  input  A3,
  input  A2,
  input  A1,
  input  A0,
  output [31:0] Output
);

  wire and_1_out, and_2_out, not_1_out;

  and and_1 (and_1_out, Enable, not_1_out);
  not not_1 (not_1_out, A4);
  and and_2 (and_2_out, Enable, A4);
  _4_x_16_decoder u_4_x_16_decoder_1 (.A4(A3), .A2(A2), .A1(A1), .A0(A0), .Enable(and_1_out), .Output(Output[15:0]));
  _4_x_16_decoder u_4_x_16_decoder_2 (.A4(A3), .A2(A2), .A1(A1), .A0(A0), .Enable(and_2_out), .Output(Output[31:16]));
endmodule

// 5 x 32
module _32_byte_ROM (
  input  [7:0] Input,
  input  Read_En,
  output [7:0] Output
);

  wire [31:0] n5_x_32_decoder_1_output;

  _5_x_32_decoder u_5_x_32_decoder_1 (
    .A4(Input[4]), .A3(Input[3]), .A2(Input[2]), .A1(Input[1]), .A0(Input[0]), .Enable(Read_En),
    .Output(n5_x_32_decoder_1_output));
  buf or_1 (Output[7], n5_x_32_decoder_1_output[0]);  // OR_Gate
  buf or_2 (Output[6], n5_x_32_decoder_1_output[0]);  // OR_Gate
  buf or_3 (Output[4], n5_x_32_decoder_1_output[0]);  // OR_Gate
  buf or_4 (Output[5], n5_x_32_decoder_1_output[0]);  // OR_Gate
  buf or_5 (Output[2], n5_x_32_decoder_1_output[0]);  // OR_Gate
  buf or_6 (Output[3], n5_x_32_decoder_1_output[0]);  // OR_Gate
  buf or_7 (Output[1], n5_x_32_decoder_1_output[0]);  // OR_Gate
  buf or_8 (Output[0], n5_x_32_decoder_1_output[0]);  // OR_Gate
endmodule

module Half_Adder (
  input  A,
  input  B,
  output Sum,
  output Carry
);

  xor xor_1 (Sum, A, B);
  and and_1 (Carry, A, B);
endmodule

module Full_Adder (
  input  A,
  input  B,
  input  Cin,
  output Sum,
  output Carry
);

  wire half_adder_1_carry, half_adder_1_sum, half_adder_2_carry;

  Half_Adder half_adder_1 (.A(A), .B(B), .Sum(half_adder_1_sum), .Carry(half_adder_1_carry));
  Half_Adder half_adder_2 (.A(half_adder_1_sum), .B(Cin), .Sum(Sum), .Carry(half_adder_2_carry));
  or or_1 (Carry, half_adder_2_carry, half_adder_1_carry);
endmodule

module _8_bit_adder (
  input  [7:0] A,
  input  [7:0] B,
  input  Sub,
  output Overflow,
  output [7:0] Output
);

  wire full_adder_1_carry, full_adder_2_carry, full_adder_3_carry, full_adder_4_carry, full_adder_5_carry,
       full_adder_6_carry, full_adder_7_carry, full_adder_8_carry, xor_2_out, xor_3_out, xor_4_out,
       xor_5_out, xor_6_out, xor_7_out, xor_8_out, xor_9_out;

  xor xor_1 (Overflow, full_adder_2_carry, full_adder_1_carry);
  xor xor_2 (xor_2_out, Sub, B[6]);
  xor xor_3 (xor_3_out, Sub, B[7]);
  Full_Adder full_adder_1 (
    .A(A[7]), .B(xor_3_out), .Cin(full_adder_2_carry), .Sum(Output[7]), .Carry(full_adder_1_carry));
  xor xor_4 (xor_4_out, Sub, B[5]);
  Full_Adder full_adder_2 (
    .A(A[6]), .B(xor_2_out), .Cin(full_adder_3_carry), .Sum(Output[6]), .Carry(full_adder_2_carry));
  Full_Adder full_adder_3 (
    .A(A[5]), .B(xor_4_out), .Cin(full_adder_4_carry), .Sum(Output[5]), .Carry(full_adder_3_carry));
  xor xor_5 (xor_5_out, Sub, B[4]);
  Full_Adder full_adder_4 (
    .A(A[4]), .B(xor_5_out), .Cin(full_adder_5_carry), .Sum(Output[4]), .Carry(full_adder_4_carry));
  xor xor_6 (xor_6_out, Sub, B[3]);
  xor xor_7 (xor_7_out, Sub, B[2]);
  Full_Adder full_adder_5 (
    .A(A[3]), .B(xor_6_out), .Cin(full_adder_6_carry), .Sum(Output[3]), .Carry(full_adder_5_carry));
  xor xor_8 (xor_8_out, Sub, B[1]);
  Full_Adder full_adder_6 (
    .A(A[2]), .B(xor_7_out), .Cin(full_adder_7_carry), .Sum(Output[2]), .Carry(full_adder_6_carry));
  Full_Adder full_adder_7 (
    .A(A[1]), .B(xor_8_out), .Cin(full_adder_8_carry), .Sum(Output[1]), .Carry(full_adder_7_carry));
  xor xor_9 (xor_9_out, Sub, B[0]);
  Full_Adder full_adder_8 (.A(A[0]), .B(xor_9_out), .Cin(Sub), .Sum(Output[0]), .Carry(full_adder_8_carry));
endmodule

module _2_x_1_mux (
  input  IN0,
  input  IN1,
  input  SEL,
  output out_4
);

  wire and_1_out, and_2_out, not_1_out;

  not not_1 (not_1_out, SEL);
  and and_1 (and_1_out, IN0, not_1_out);
  and and_2 (and_2_out, IN1, SEL);
  or or_1 (out_4, and_1_out, and_2_out);
endmodule

module register_file (
  input  Clk,
  input  WriteEn,
  input  [31:0] WriteData,
  input  [1:0] WriteAdr,
  input  [1:0] ReadAdr1,
  input  [1:0] ReadAdr2,
  output [31:0] Read1,
  output [31:0] Read2
);

  wire and_1_out, and_2_out, and_3_out, and_4_out, clock_1_out, n2_x_4_decoder_1_d0, n2_x_4_decoder_1_d1,
       n2_x_4_decoder_1_d2, n2_x_4_decoder_1_d3;

  Clock clock_1 (.out(clock_1_out));
  _2_x_4_decoder u_2_x_4_decoder_1 (
    .En(WriteEn), .A(WriteAdr[1]), .B(WriteAdr[0]), .D0(n2_x_4_decoder_1_d0), .D1(n2_x_4_decoder_1_d1),
    .D2(n2_x_4_decoder_1_d2), .D3(n2_x_4_decoder_1_d3));
  _2_x_4_decoder u_2_x_4_decoder_2 (.En(1'b1), .A(ReadAdr1[1]), .B(ReadAdr1[0]));  // open: D0, D1, D2, D3
  and and_1 (and_1_out, WriteEn, n2_x_4_decoder_1_d0);
  and and_2 (and_2_out, WriteEn, n2_x_4_decoder_1_d1);
  and and_3 (and_3_out, WriteEn, n2_x_4_decoder_1_d2);
  and and_4 (and_4_out, WriteEn, n2_x_4_decoder_1_d3);
  _32_bit_register u_32_bit_register_1 (
    .Clk(clock_1_out), .Write_En(and_1_out), .Input(WriteData));  // open: Clear, Output
  _32_bit_register u_32_bit_register_2 (
    .Clk(clock_1_out), .Write_En(and_2_out), .Input(WriteData));  // open: Clear, Output
  _32_bit_register u_32_bit_register_3 (
    .Clk(clock_1_out), .Write_En(and_3_out), .Input(WriteData));  // open: Clear, Output
  _32_bit_register u_32_bit_register_4 (
    .Clk(clock_1_out), .Write_En(and_4_out), .Input(WriteData));  // open: Clear, Output
  _2_x_4_decoder u_2_x_4_decoder_3 (.En(1'b1), .A(ReadAdr2[1]), .B(ReadAdr2[0]));  // open: D0, D1, D2, D3
endmodule

module _32_bit_register (
  input  Clk,
  input  Write_En,
  input  Clear,
  input  [31:0] Input,
  output [31:0] Output
);

  wire and_1_out, and_2_out, and_3_out, and_4_out, and_5_out, and_6_out, and_7_out, and_8_out, and_9_out,
       and_10_out, and_11_out, and_12_out, and_13_out, and_14_out, and_15_out, and_16_out, and_17_out,
       and_18_out, and_19_out, and_20_out, and_21_out, and_22_out, and_23_out, and_24_out, and_25_out,
       and_26_out, and_27_out, and_28_out, and_29_out, and_30_out, and_31_out, and_32_out, and_33_out,
       and_34_out, and_35_out, and_36_out, and_37_out, and_38_out, and_39_out, and_40_out, and_41_out,
       and_42_out, and_43_out, and_44_out, and_45_out, and_46_out, and_47_out, and_48_out, and_49_out,
       and_50_out, and_51_out, and_52_out, and_53_out, and_54_out, and_55_out, and_56_out, and_57_out,
       and_58_out, and_59_out, and_60_out, and_61_out, and_62_out, and_63_out, and_64_out, not_1_out,
       not_2_out, or_1_out, or_2_out, or_3_out, or_4_out, or_5_out, or_6_out, or_7_out, or_8_out, or_9_out,
       or_10_out, or_11_out, or_12_out, or_13_out, or_14_out, or_15_out, or_16_out, or_17_out, or_18_out,
       or_19_out, or_20_out, or_21_out, or_22_out, or_23_out, or_24_out, or_25_out, or_26_out, or_27_out,
       or_28_out, or_29_out, or_30_out, or_31_out, or_32_out;

  not not_1 (not_1_out, Clear);
  not not_2 (not_2_out, Write_En);
  and and_1 (and_1_out, Input[7], Write_En, not_1_out);
  and and_2 (and_2_out, Input[6], Write_En, not_1_out);
  and and_3 (and_3_out, Input[5], Write_En, not_1_out);
  and and_4 (and_4_out, Input[4], Write_En, not_1_out);
  and and_5 (and_5_out, Input[3], Write_En, not_1_out);
  and and_6 (and_6_out, Input[2], Write_En, not_1_out);
  and and_7 (and_7_out, Input[1], Write_En, not_1_out);
  and and_8 (and_8_out, Input[0], Write_En, not_1_out);
  and and_9 (and_9_out, Input[15], Write_En, not_1_out);
  and and_10 (and_10_out, Input[14], Write_En, not_1_out);
  and and_11 (and_11_out, Input[13], Write_En, not_1_out);
  and and_12 (and_12_out, Input[12], Write_En, not_1_out);
  and and_13 (and_13_out, Input[11], Write_En, not_1_out);
  and and_14 (and_14_out, Input[10], Write_En, not_1_out);
  and and_15 (and_15_out, Input[9], Write_En, not_1_out);
  and and_16 (and_16_out, Input[8], Write_En, not_1_out);
  and and_17 (and_17_out, Input[23], Write_En, not_1_out);
  and and_18 (and_18_out, Input[22], Write_En, not_1_out);
  and and_19 (and_19_out, Input[21], Write_En, not_1_out);
  and and_20 (and_20_out, Input[20], Write_En, not_1_out);
  and and_21 (and_21_out, Input[19], Write_En, not_1_out);
  and and_22 (and_22_out, Input[18], Write_En, not_1_out);
  and and_23 (and_23_out, Input[17], Write_En, not_1_out);
  and and_24 (and_24_out, Input[16], Write_En, not_1_out);
  and and_25 (and_25_out, Input[31], Write_En, not_1_out);
  and and_26 (and_26_out, Input[30], Write_En, not_1_out);
  and and_27 (and_27_out, Input[29], Write_En, not_1_out);
  and and_28 (and_28_out, Input[28], Write_En, not_1_out);
  and and_29 (and_29_out, Input[27], Write_En, not_1_out);
  and and_30 (and_30_out, Input[26], Write_En, not_1_out);
  and and_31 (and_31_out, Input[25], Write_En, not_1_out);
  and and_32 (and_32_out, Input[24], Write_En, not_1_out);
  and and_33 (and_33_out, not_2_out, not_1_out, Output[7]);
  and and_34 (and_34_out, not_2_out, not_1_out, Output[6]);
  and and_35 (and_35_out, not_2_out, not_1_out, Output[5]);
  and and_36 (and_36_out, not_2_out, not_1_out, Output[4]);
  and and_37 (and_37_out, not_2_out, not_1_out, Output[3]);
  and and_38 (and_38_out, not_2_out, not_1_out, Output[2]);
  and and_39 (and_39_out, not_2_out, not_1_out, Output[1]);
  and and_40 (and_40_out, not_2_out, not_1_out, Output[0]);
  and and_41 (and_41_out, not_2_out, not_1_out, Output[15]);
  and and_42 (and_42_out, not_2_out, not_1_out, Output[14]);
  and and_43 (and_43_out, not_2_out, not_1_out, Output[13]);
  and and_44 (and_44_out, not_2_out, not_1_out, Output[12]);
  and and_45 (and_45_out, not_2_out, not_1_out, Output[11]);
  and and_46 (and_46_out, not_2_out, not_1_out, Output[10]);
  and and_47 (and_47_out, not_2_out, not_1_out, Output[9]);
  and and_48 (and_48_out, not_2_out, not_1_out, Output[8]);
  and and_49 (and_49_out, not_2_out, not_1_out, Output[23]);
  and and_50 (and_50_out, not_2_out, not_1_out, Output[22]);
  and and_51 (and_51_out, not_2_out, not_1_out, Output[21]);
  and and_52 (and_52_out, not_2_out, not_1_out, Output[20]);
  and and_53 (and_53_out, not_2_out, not_1_out, Output[19]);
  and and_54 (and_54_out, not_2_out, not_1_out, Output[18]);
  and and_55 (and_55_out, not_2_out, not_1_out, Output[17]);
  and and_56 (and_56_out, not_2_out, not_1_out, Output[16]);
  and and_57 (and_57_out, not_2_out, not_1_out, Output[31]);
  and and_58 (and_58_out, not_2_out, not_1_out, Output[30]);
  and and_59 (and_59_out, not_2_out, not_1_out, Output[29]);
  and and_60 (and_60_out, not_2_out, not_1_out, Output[28]);
  and and_61 (and_61_out, not_2_out, not_1_out, Output[27]);
  and and_62 (and_62_out, not_2_out, not_1_out, Output[26]);
  and and_63 (and_63_out, not_2_out, not_1_out, Output[25]);
  and and_64 (and_64_out, not_2_out, not_1_out, Output[24]);
  or or_1 (or_1_out, and_1_out, and_33_out);
  or or_2 (or_2_out, and_2_out, and_34_out);
  or or_3 (or_3_out, and_3_out, and_35_out);
  or or_4 (or_4_out, and_4_out, and_36_out);
  or or_5 (or_5_out, and_5_out, and_37_out);
  or or_6 (or_6_out, and_6_out, and_38_out);
  or or_7 (or_7_out, and_7_out, and_39_out);
  or or_8 (or_8_out, and_8_out, and_40_out);
  or or_9 (or_9_out, and_9_out, and_41_out);
  or or_10 (or_10_out, and_10_out, and_42_out);
  or or_11 (or_11_out, and_11_out, and_43_out);
  or or_12 (or_12_out, and_12_out, and_44_out);
  or or_13 (or_13_out, and_13_out, and_45_out);
  or or_14 (or_14_out, and_14_out, and_46_out);
  or or_15 (or_15_out, and_15_out, and_47_out);
  or or_16 (or_16_out, and_16_out, and_48_out);
  or or_17 (or_17_out, and_17_out, and_49_out);
  or or_18 (or_18_out, and_18_out, and_50_out);
  or or_19 (or_19_out, and_19_out, and_51_out);
  or or_20 (or_20_out, and_20_out, and_52_out);
  or or_21 (or_21_out, and_21_out, and_53_out);
  or or_22 (or_22_out, and_22_out, and_54_out);
  or or_23 (or_23_out, and_23_out, and_55_out);
  or or_24 (or_24_out, and_24_out, and_56_out);
  or or_25 (or_25_out, and_25_out, and_57_out);
  or or_26 (or_26_out, and_26_out, and_58_out);
  or or_27 (or_27_out, and_27_out, and_59_out);
  or or_28 (or_28_out, and_28_out, and_60_out);
  or or_29 (or_29_out, and_29_out, and_61_out);
  or or_30 (or_30_out, and_30_out, and_62_out);
  or or_31 (or_31_out, and_31_out, and_63_out);
  or or_32 (or_32_out, and_32_out, and_64_out);
  D_FF d_ff_1 (.D(or_1_out), .Clk(Clk), .Q(Output[7]));
  D_FF d_ff_2 (.D(or_2_out), .Clk(Clk), .Q(Output[6]));
  D_FF d_ff_3 (.D(or_3_out), .Clk(Clk), .Q(Output[5]));
  D_FF d_ff_4 (.D(or_4_out), .Clk(Clk), .Q(Output[4]));
  D_FF d_ff_5 (.D(or_5_out), .Clk(Clk), .Q(Output[3]));
  D_FF d_ff_6 (.D(or_6_out), .Clk(Clk), .Q(Output[2]));
  D_FF d_ff_7 (.D(or_7_out), .Clk(Clk), .Q(Output[1]));
  D_FF d_ff_8 (.D(or_8_out), .Clk(Clk), .Q(Output[0]));
  D_FF d_ff_9 (.D(or_9_out), .Clk(Clk), .Q(Output[15]));
  D_FF d_ff_10 (.D(or_10_out), .Clk(Clk), .Q(Output[14]));
  D_FF d_ff_11 (.D(or_11_out), .Clk(Clk), .Q(Output[13]));
  D_FF d_ff_12 (.D(or_12_out), .Clk(Clk), .Q(Output[12]));
  D_FF d_ff_13 (.D(or_13_out), .Clk(Clk), .Q(Output[11]));
  D_FF d_ff_14 (.D(or_14_out), .Clk(Clk), .Q(Output[10]));
  D_FF d_ff_15 (.D(or_15_out), .Clk(Clk), .Q(Output[9]));
  D_FF d_ff_16 (.D(or_16_out), .Clk(Clk), .Q(Output[8]));
  D_FF d_ff_17 (.D(or_17_out), .Clk(Clk), .Q(Output[23]));
  D_FF d_ff_18 (.D(or_18_out), .Clk(Clk), .Q(Output[22]));
  D_FF d_ff_19 (.D(or_19_out), .Clk(Clk), .Q(Output[21]));
  D_FF d_ff_20 (.D(or_20_out), .Clk(Clk), .Q(Output[20]));
  D_FF d_ff_21 (.D(or_21_out), .Clk(Clk), .Q(Output[19]));
  D_FF d_ff_22 (.D(or_22_out), .Clk(Clk), .Q(Output[18]));
  D_FF d_ff_23 (.D(or_23_out), .Clk(Clk), .Q(Output[17]));
  D_FF d_ff_24 (.D(or_24_out), .Clk(Clk), .Q(Output[16]));
  D_FF d_ff_25 (.D(or_25_out), .Clk(Clk), .Q(Output[31]));
  D_FF d_ff_26 (.D(or_26_out), .Clk(Clk), .Q(Output[30]));
  D_FF d_ff_27 (.D(or_27_out), .Clk(Clk), .Q(Output[29]));
  D_FF d_ff_28 (.D(or_28_out), .Clk(Clk), .Q(Output[28]));
  D_FF d_ff_29 (.D(or_29_out), .Clk(Clk), .Q(Output[27]));
  D_FF d_ff_30 (.D(or_30_out), .Clk(Clk), .Q(Output[26]));
  D_FF d_ff_31 (.D(or_31_out), .Clk(Clk), .Q(Output[25]));
  D_FF d_ff_32 (.D(or_32_out), .Clk(Clk), .Q(Output[24]));

  // Notes on the sheet:
  //   Little Endian
endmodule
